# Fritzing sketch devboard (saved by Fritzing 0.9.3b)

parts:
  4_8V = 4 x AAA Battery Mount
  U1 = NodeMCU V3.0
  Part1 = InvenSense MPU6050
  C1 = Capacitor [package=0805]
  C2 = Capacitor [package=0805]

nets:
  GND: 4_8V.-, U1.GND, Part1.GND, C1.2, C2.2
  N1: 4_8V.+, U1.Vin
  N2: U1.D1, Part1.SCL, C1.1
  N3: U1.D2, Part1.SDA, C2.1
  3V3: U1.3V3, Part1.VCC

custom parts:
  NodeMCU V3.0: ESP8266 based NodeMCU
