# Fritzing sketch schematic (saved by Fritzing 0.9.3b)

parts:
  WeMos_D1_Mini1 = WeMos D1 Mini
  Part1 = InvenSense MPU6050
  4_8V = 4 x AAA Battery Mount
  C3 = Capacitor [package=0805]
  C4 = Capacitor [package=0805]

nets:
  3V3: WeMos_D1_Mini1.3V3, Part1.VCC
  N1: WeMos_D1_Mini1.5V, 4_8V.+
  N2: WeMos_D1_Mini1.D1, Part1.SCL, C4.1
  N3: WeMos_D1_Mini1.D2, Part1.SDA, C3.1
  N4: WeMos_D1_Mini1.G, Part1.GND, 4_8V.-, C3.2, C4.2

notes:
  400pF
